// Logisim project sap1_ben_eater.circ as structural Verilog: 2 circuits, main circuit main
module _8_bit_register (
  input  in_1,
  input  in_2,
  input  in_3,
  input  in_4,
  input  in_5,
  input  in_6,
  input  in_7,
  input  in_8,
  input  in_9,
  input  in_10,
  input  in_11
);

  wire [7:0] register_1_q;

  Register #(.trigger("high")) register_1 (
    .D({in_8, in_7, in_6, in_5, in_4, in_3, in_2, in_1}), .en(in_9), .Q(register_1_q), .clk(in_10),
    .clr(in_11));
  LED led_1 (.in(register_1_q[0]));
  LED led_2 (.in(register_1_q[1]));
  LED led_3 (.in(register_1_q[2]));
  LED led_4 (.in(register_1_q[3]));
  LED led_5 (.in(register_1_q[4]));
  LED led_6 (.in(register_1_q[5]));
  LED led_7 (.in(register_1_q[6]));
  LED led_8 (.in(register_1_q[7]));
endmodule

module main (
  input  Run_Step,
  input  ADDR,
  input  in_3,
  input  in_4,
  input  in_5,
  input  in_6,
  input  in_7,
  input  in_8,
  input  in_9,
  input  in_10,
  input  Value,
  input  in_12,
  input  in_13,
  input  in_14,
  input  in_15,
  input  in_16,
  input  in_17,
  input  in_18,
  input  in_19,
  input  in_20,
  input  in_21,
  input  in_22,
  input  in_23,
  input  in_24,
  input  in_25,
  input  in_26,
  input  in_27,
  input  in_28,
  input  in_29,
  input  in_30,
  input  in_31,
  input  in_32,
  input  in_33
);

  wire AI, AO, BI, button_1_out, button_3_out, CE, CLK, clock_1_out, CO, controlled_buffer_17_out,
       decoder_1_out5, EO, HLT, II, IO, J, JC, JMP, MI, not_1_out, not_2_out, not_3_out, not_4_out,
       not_5_out, not_6_out, OI, or_1_out, RI, RO, RST, SU;
  wire [2:0] counter_1_q;
  wire [3:0] counter_2_q, multiplexer_3_out, register_1_q;
  wire [7:0] adder_1_out, BUS, controlled_buffer_22_out, controlled_inverter_1_out, multiplexer_2_out,
       ram_1_data, register_2_q, register_3_q, register_4_q, register_5_q;
  wire [23:0] rom_1_data;
  wire [31:0] rom_2_data;

  assign HLT = in_8 ? in_9 : 1'bz;  // Controlled_Buffer controlled_buffer_1
  assign MI = in_8 ? in_10 : 1'bz;  // Controlled_Buffer controlled_buffer_2
  assign RI = in_8 ? in_19 : 1'bz;  // Controlled_Buffer controlled_buffer_3
  assign RO = in_8 ? in_20 : 1'bz;  // Controlled_Buffer controlled_buffer_4
  assign IO = in_8 ? in_21 : 1'bz;  // Controlled_Buffer controlled_buffer_5
  assign II = in_8 ? in_22 : 1'bz;  // Controlled_Buffer controlled_buffer_6
  assign AI = in_8 ? in_23 : 1'bz;  // Controlled_Buffer controlled_buffer_7
  assign AO = in_8 ? in_24 : 1'bz;  // Controlled_Buffer controlled_buffer_8
  assign EO = in_8 ? in_25 : 1'bz;  // Controlled_Buffer controlled_buffer_9
  assign SU = in_8 ? in_26 : 1'bz;  // Controlled_Buffer controlled_buffer_10
  assign BI = in_8 ? in_27 : 1'bz;  // Controlled_Buffer controlled_buffer_11
  assign OI = in_8 ? in_28 : 1'bz;  // Controlled_Buffer controlled_buffer_12
  assign CE = in_8 ? in_29 : 1'bz;  // Controlled_Buffer controlled_buffer_13
  assign CO = in_8 ? in_30 : 1'bz;  // Controlled_Buffer controlled_buffer_14
  assign J = in_8 ? in_31 : 1'bz;  // Controlled_Buffer controlled_buffer_15
  assign JC = in_8 ? in_32 : 1'bz;  // Controlled_Buffer controlled_buffer_16
  LED led_1 (.in(counter_1_q[2]));
  not not_1 (not_1_out, HLT);
  Clock clock_1 (.out(clock_1_out));
  Multiplexer multiplexer_1 (.in0(clock_1_out), .in1(button_1_out), .out(CLK), .sel(Run_Step), .en(not_1_out));
  Button button_1 (.out(button_1_out));
  Multiplexer #(.width(8)) multiplexer_2 (
    .in0(BUS), .in1({Value, in_12, in_13, in_14, in_15, in_16, in_17, in_18}), .out(multiplexer_2_out),
    .sel(not_2_out), .en(1'b1));
  not not_2 (not_2_out, in_6);
  LED led_2 (.in(counter_1_q[1]));
  LED led_3 (.in(counter_1_q[0]));
  Decoder #(.select(3)) decoder_1 (
    .out5(decoder_1_out5), .sel(counter_1_q), .en(1'b1));  // open: out0, out1, out2, out3, out4, out6, out7
  Counter #(.width(3), .max('h7), .ongoal("continue"), .trigger("falling")) counter_1 (
    .count(1'b1), .Q(counter_1_q), .clk(CLK), .clr(or_1_out));  // open: load, D, carry
  or or_1 (or_1_out, RST, decoder_1_out5);
  LED #(.active("false")) led_4 (.in(in_6));
  LED led_5 (.in(in_6));
  Multiplexer #(.width(4)) multiplexer_3 (
    .in0({ADDR, in_3, in_4, in_5}), .in1(register_1_q), .out(multiplexer_3_out), .sel(in_6), .en(1'b1));
  Register #(.width(4)) register_1 (.D(BUS[3:0]), .en(MI), .Q(register_1_q), .clk(CLK), .clr(RST));
  Register register_2 (.D(BUS), .en(II), .Q(register_2_q), .clk(CLK), .clr(RST));
  Button button_2 (.out(RST));
  Pull_Resistor pull_resistor_1 (.node(RST));
  LED led_6 (.in(multiplexer_3_out[1]));
  LED led_7 (.in(multiplexer_3_out[3]));
  LED led_8 (.in(multiplexer_3_out[2]));
  LED led_9 (.in(multiplexer_3_out[0]));
  assign controlled_buffer_17_out = RI ? CLK : 1'bz;  // Controlled_Buffer controlled_buffer_17
  Pull_Resistor pull_resistor_2 (.node(controlled_buffer_17_out));
  assign BUS = IO ? {4'b0000, register_2_q[3:0]} : 8'bz;  // Controlled_Buffer controlled_buffer_18
  RAM #(.addrWidth(4), .bus("separate")) ram_1 (
    .addr(multiplexer_3_out), .din(multiplexer_2_out), .data(ram_1_data), .str(controlled_buffer_17_out),
    .sel(1'b1), .clk(controlled_buffer_17_out), .ld(not_3_out), .clr(1'b0));
  not not_3 (not_3_out, controlled_buffer_17_out);
  assign controlled_buffer_17_out = button_3_out ? 1'b1 : 1'bz;  // Controlled_Buffer controlled_buffer_19
  LED led_10 (.in(ram_1_data[5]));
  LED led_11 (.in(ram_1_data[4]));
  LED led_12 (.in(ram_1_data[7]));
  LED led_13 (.in(ram_1_data[6]));
  LED led_14 (.in(register_2_q[5]));
  LED led_15 (.in(register_2_q[6]));
  LED led_16 (.in(register_2_q[4]));
  LED led_17 (.in(register_2_q[7]));
  assign BUS = RO ? ram_1_data : 8'bz;  // Controlled_Buffer controlled_buffer_20
  Button button_3 (.out(button_3_out));
  LED led_18 (.in(ram_1_data[1]));
  LED led_19 (.in(ram_1_data[0]));
  LED led_20 (.in(ram_1_data[2]));
  LED led_21 (.in(ram_1_data[3]));
  LED led_22 (.in(register_2_q[3]));
  LED led_23 (.in(register_2_q[1]));
  LED led_24 (.in(register_2_q[2]));
  LED led_25 (.in(register_2_q[0]));
  ROM #(.addrWidth(7), .dataWidth(24)) rom_1 (.addr({register_2_q[7:4], counter_1_q}), .data(rom_1_data), .sel(1'b1));
  LED led_26 (.in(BUS[7]));
  LED led_27 (.in(BUS[5]));
  LED led_28 (.in(BUS[6]));
  Pull_Resistor pull_resistor_3 (.node(BUS));
  assign BUS = in_7 ? {8{1'b1}} : 8'bz;  // Controlled_Buffer controlled_buffer_21
  not not_4 (not_4_out, in_8);
  assign {HLT, MI, RI, RO, IO, II, AI, AO, EO, SU, BI, OI, CE, CO, J, JC, controlled_buffer_22_out} = not_4_out ? rom_1_data : 24'bz;  // Controlled_Buffer controlled_buffer_22
  LED led_29 (.in(BUS[2]));
  LED led_30 (.in(BUS[1]));
  LED led_31 (.in(BUS[3]));
  LED led_32 (.in(BUS[4]));
  LED led_33 (.in(BUS[0]));
  LED led_34 (.in(HLT));
  Counter #(.width(4), .max('hf), .ongoal("continue")) counter_2 (
    .load(JMP), .D(BUS[3:0]), .count(CE), .Q(counter_2_q), .clk(CLK), .clr(RST));  // open: carry
  assign BUS = AO ? register_4_q : 8'bz;  // Controlled_Buffer controlled_buffer_23
  assign BUS = 1'b0 ? register_5_q : 8'bz;  // Controlled_Buffer controlled_buffer_24
  Register register_3 (.D(BUS), .en(OI), .Q(register_3_q), .clk(CLK), .clr(RST));
  LED led_35 (.in(RO));
  LED led_36 (.in(RI));
  LED led_37 (.in(IO));
  LED led_38 (.in(MI));
  LED led_39 (.in(counter_2_q[0]));
  LED led_40 (.in(counter_2_q[2]));
  LED led_41 (.in(counter_2_q[3]));
  LED led_42 (.in(counter_2_q[1]));
  assign BUS[3:0] = CO ? counter_2_q : 4'bz;  // Controlled_Buffer controlled_buffer_25
  LED led_43 (.in(register_4_q[7]));
  LED led_44 (.in(register_4_q[6]));
  Register register_4 (.D(BUS), .en(AI), .Q(register_4_q), .clk(CLK), .clr(RST));
  assign controlled_inverter_1_out = SU ? ~register_5_q : 8'bz;  // Controlled_Inverter controlled_inverter_1
  not not_5 (not_5_out, SU);
  assign controlled_inverter_1_out = not_5_out ? register_5_q : 8'bz;  // Controlled_Buffer controlled_buffer_26
  LED led_45 (.in(register_5_q[6]));
  LED led_46 (.in(register_5_q[7]));
  Register register_5 (.D(BUS), .en(BI), .Q(register_5_q), .clk(CLK), .clr(RST));
  LED led_47 (.in(EO));
  LED led_48 (.in(AO));
  LED led_49 (.in(AI));
  LED led_50 (.in(II));
  LED led_51 (.in(register_4_q[4]));
  LED led_52 (.in(register_4_q[5]));
  LED led_53 (.in(register_4_q[2]));
  LED led_54 (.in(register_4_q[3]));
  Adder adder_1 (.a(register_4_q), .b(controlled_inverter_1_out), .out(adder_1_out), .cin(SU));  // open: cout
  LED led_55 (.in(register_5_q[4]));
  LED led_56 (.in(register_5_q[5]));
  LED led_57 (.in(register_5_q[3]));
  LED led_58 (.in(register_5_q[2]));
  ROM #(.addrWidth(9), .dataWidth(32)) rom_2 (.addr({in_33, register_3_q}), .data(rom_2_data), .sel(1'b1));
  LED led_59 (.in(OI));
  LED led_60 (.in(CE));
  LED led_61 (.in(BI));
  LED led_62 (.in(SU));
  LED led_63 (.in(register_4_q[0]));
  LED led_64 (.in(register_4_q[1]));
  assign JMP = JC ? register_4_q[7] : 1'bz;  // Controlled_Buffer controlled_buffer_27
  LED led_65 (.in(adder_1_out[4]));
  LED led_66 (.in(adder_1_out[7]));
  LED led_67 (.in(adder_1_out[5]));
  LED led_68 (.in(adder_1_out[6]));
  assign BUS = EO ? adder_1_out : 8'bz;  // Controlled_Buffer controlled_buffer_28
  LED led_69 (.in(register_5_q[0]));
  LED led_70 (.in(register_5_q[1]));
  LED led_71 (.in(J));
  LED led_72 (.in(JC));
  LED led_73 (.in(CO));
  assign JMP = not_6_out ? J : 1'bz;  // Controlled_Buffer controlled_buffer_29
  not not_6 (not_6_out, JC);
  LED led_74 (.in(adder_1_out[2]));
  LED led_75 (.in(adder_1_out[0]));
  LED led_76 (.in(adder_1_out[1]));
  LED led_77 (.in(adder_1_out[3]));
  _7_Segment_Display u_7_segment_display_1 (
    .g(rom_2_data[27]), .f(rom_2_data[26]), .a(rom_2_data[25]), .b(rom_2_data[24]), .e(rom_2_data[31]),
    .d(rom_2_data[30]), .c(rom_2_data[29]), .dp(rom_2_data[28]));
  _7_Segment_Display u_7_segment_display_2 (
    .g(rom_2_data[19]), .f(rom_2_data[18]), .a(rom_2_data[17]), .b(rom_2_data[16]), .e(rom_2_data[23]),
    .d(rom_2_data[22]), .c(rom_2_data[21]), .dp(rom_2_data[20]));
  _7_Segment_Display u_7_segment_display_3 (
    .g(rom_2_data[11]), .f(rom_2_data[10]), .a(rom_2_data[9]), .b(rom_2_data[8]), .e(rom_2_data[15]),
    .d(rom_2_data[14]), .c(rom_2_data[13]), .dp(rom_2_data[12]));
  _7_Segment_Display u_7_segment_display_4 (
    .g(rom_2_data[3]), .f(rom_2_data[2]), .a(rom_2_data[1]), .b(rom_2_data[0]), .e(rom_2_data[7]),
    .d(rom_2_data[6]), .c(rom_2_data[5]), .dp(rom_2_data[4]));

  // Other names for the same wires on the sheet: MANUAL = in_8; PRGM_RUN = in_6

  // Notes on the sheet:
  //   Step
  //   Instruction Register
  //   Microcode Counter
  //   RAM Contents
  //   Instruction ROM
  //   LOAD
  //   contents of rom_1 (hex, n*v repeats v):
  //   400400 140800 6*0 400400 140800 480000 120000 4*0 400400 140800 480000 102000 28000 0 0 0 400400
  //   140800 480000 102000 2c000 0 0 0 400400 140800 480000 210000 4*0 400400 140800 a0000 5*0 400400
  //   140800 80200 5*0 400400 140800 80100 5*0 400400 140800 6*0 400400 140800 6*0 400400 140800 6*0
  //   400400 140800 6*0 400400 140800 6*0 400400 140800 6*0 400400 140800 11000 5*0 400400 140800 800000
  //   A Register
  //   Output Register
  //   Control Word
  //   Program Counter
  //   ALU
  //   B Register
  //   Output ROM
  //   contents of rom_2 (hex, n*v repeats v):
  //   e7 21 cb 6b 2d 6e ee 23 ef 6f 21e7 2121 21cb 216b 212d 216e 21ee 2123 21ef 216f cbe7 cb21 cbcb cb6b
  //   cb2d cb6e cbee cb23 cbef cb6f 6be7 6b21 6bcb 6b6b 6b2d 6b6e 6bee 6b23 6bef 6b6f 2de7 2d21 2dcb 2d6b
  //   2d2d 2d6e 2dee 2d23 2def 2d6f 6ee7 6e21 6ecb 6e6b 6e2d 6e6e 6eee 6e23 6eef 6e6f eee7 ee21 eecb ee6b
  //   ee2d ee6e eeee ee23 eeef ee6f 23e7 2321 23cb 236b 232d 236e 23ee 2323 23ef 236f efe7 ef21 efcb ef6b
  //   ef2d ef6e efee ef23 efef ef6f 6fe7 6f21 6fcb 6f6b 6f2d 6f6e 6fee 6f23 6fef 6f6f 21e7e7 21e721 21e7cb
  //   21e76b 21e72d 21e76e 21e7ee 21e723 21e7ef 21e76f 2121e7 212121 2121cb 21216b 21212d 21216e 2121ee
  //   212123 2121ef 21216f 21cbe7 21cb21 21cbcb 21cb6b 21cb2d 21cb6e 21cbee 21cb23 21cbef 21cb6f 216be7
  //   216b21 216bcb 216b6b 216b2d 216b6e 216bee 216b23 216bef 216b6f 212de7 212d21 212dcb 212d6b 212d2d
  //   212d6e 212dee 212d23 212def 212d6f 216ee7 216e21 216ecb 216e6b 216e2d 216e6e 216eee 216e23 216eef
  //   216e6f 21eee7 21ee21 21eecb 21ee6b 21ee2d 21ee6e 21eeee 21ee23 21eeef 21ee6f 2123e7 212321 2123cb
  //   21236b 21232d 21236e 2123ee 212323 2123ef 21236f 21efe7 21ef21 21efcb 21ef6b 21ef2d 21ef6e 21efee
  //   21ef23 21efef 21ef6f 216fe7 216f21 216fcb 216f6b 216f2d 216f6e 216fee 216f23 216fef 216f6f cbe7e7
  //   cbe721 cbe7cb cbe76b cbe72d cbe76e cbe7ee cbe723 cbe7ef cbe76f cb21e7 cb2121 cb21cb cb216b cb212d
  //   cb216e cb21ee cb2123 cb21ef cb216f cbcbe7 cbcb21 cbcbcb cbcb6b cbcb2d cbcb6e cbcbee cbcb23 cbcbef
  //   cbcb6f cb6be7 cb6b21 cb6bcb cb6b6b cb6b2d cb6b6e cb6bee cb6b23 cb6bef cb6b6f cb2de7 cb2d21 cb2dcb
  //   cb2d6b cb2d2d cb2d6e cb2dee cb2d23 cb2def cb2d6f cb6ee7 cb6e21 cb6ecb cb6e6b cb6e2d cb6e6e e7 21 cb
  //   6b 2d 6e ee 23 ef 6f 21e7 2121 21cb 216b 212d 216e 21ee 2123 21ef 216f cbe7 cb21 cbcb cb6b cb2d cb6e
  //   cbee cb23 cbef cb6f 6be7 6b21 6bcb 6b6b 6b2d 6b6e 6bee 6b23 6bef 6b6f 2de7 2d21 2dcb 2d6b 2d2d 2d6e
  //   2dee 2d23 2def 2d6f 6ee7 6e21 6ecb 6e6b 6e2d 6e6e 6eee 6e23 6eef 6e6f eee7 ee21 eecb ee6b ee2d ee6e
  //   eeee ee23 eeef ee6f 23e7 2321 23cb 236b 232d 236e 23ee 2323 23ef 236f efe7 ef21 efcb ef6b ef2d ef6e
  //   efee ef23 efef ef6f 6fe7 6f21 6fcb 6f6b 6f2d 6f6e 6fee 6f23 6fef 6f6f 21e7e7 21e721 21e7cb 21e76b
  //   21e72d 21e76e 21e7ee 21e723 21e7ef 21e76f 2121e7 212121 2121cb 21216b 21212d 21216e 2121ee 212123
  //   2121ef 21216f 21cbe7 21cb21 21cbcb 21cb6b 21cb2d 21cb6e 21cbee 21cb23 821cbef 821cb23 821cbee
  //   821cb6e 821cb2d 821cb6b 821cbcb 821cb21 821cbe7 821216f 82121ef 8212123 82121ee 821216e 821212d
  //   821216b 82121cb 8212121 82121e7 821e76f 821e7ef 821e723 821e7ee 821e76e 821e72d 821e76b 821e7cb
  //   821e721 821e7e7 8006f6f 8006fef 8006f23 8006fee 8006f6e 8006f2d 8006f6b 8006fcb 8006f21 8006fe7
  //   800ef6f 800efef 800ef23 800efee 800ef6e 800ef2d 800ef6b 800efcb 800ef21 800efe7 800236f 80023ef
  //   8002323 80023ee 800236e 800232d 800236b 80023cb 8002321 80023e7 800ee6f 800eeef 800ee23 800eeee
  //   800ee6e 800ee2d 800ee6b 800eecb 800ee21 800eee7 8006e6f 8006eef 8006e23 8006eee 8006e6e 8006e2d
  //   8006e6b 8006ecb 8006e21 8006ee7 8002d6f 8002def 8002d23 8002dee 8002d6e 8002d2d 8002d6b 8002dcb
  //   8002d21 8002de7 8006b6f 8006bef 8006b23 8006bee 8006b6e 8006b2d 8006b6b 8006bcb 8006b21 8006be7
  //   800cb6f 800cbef 800cb23 800cbee 800cb6e 800cb2d 800cb6b 800cbcb 800cb21 800cbe7 800216f 80021ef
  //   8002123 80021ee 800216e 800212d 800216b 80021cb 8002121 80021e7 800006f 80000ef 8000023 80000ee
  //   800006e 800002d 800006b 80000cb 8000021
endmodule
